# Fritzing sketch Treppenlicht (saved by Fritzing 0.9.2b)
stripboards: 2
perfboards: 1

parts:
  IC1 = IC, DIP package, 28 pins [chip_label=PIC32MX150F128B]  # not connected
  D1 = Rectifier Diode [part_number=1N4001 package="300 mil [THT]"]
  U1 = Voltage Regulator - Variable [part_number=LM317 package="TO220 [THT]"]
  C1 = Electrolytic Capacitor [capacitance=100µF package="100 mil [THT, electrolytic]"]
  C2 = Ceramic Capacitor [capacitance=100nF package="100 mil [THT, multilayer]"]
  R3 = Resistor [tolerance=±5% resistance=1k package=THT]
  R4 = Resistor [tolerance=±5% resistance=1.6k package=THT]
  C4 = Electrolytic Capacitor [capacitance=100µF package="100 mil [THT, electrolytic]"]

nets:
  12V: D1.cathode, U1.IN, C1.+, C2.1
  N1: U1.ADJ, R3.Pin_1, R4.Pin_0
  3.3V: U1.OUT, R3.Pin_0, C4.+
  GND: C1.-, C2.0, R4.Pin_1, C4.-
